# Fritzing sketch ATTEMPT3-SENG-218-9-6 (saved by Fritzing 0.9.3b)
breadboards: 3

parts:
  IC3 = Voltage Regulator [package=to220-igo]
  U15 = 555 Timer [package="DIP8 [THT]"]
  U16 = 555 Timer [package="DIP8 [THT]"]
  U17 = 555 Timer [package="DIP8 [THT]"]
  U18 = IC, DIP package, 16 pins [chip_label=SN74163J]
  U19 = IC, DIP package, 16 pins [chip_label=SN74LS138N]
  U20 = IC, DIP package, 14 pins [chip_label=7406]
  U22 = IC, DIP package, 14 pins [chip_label=SN74LS08N]
  U21 = IC, DIP package, 14 pins [chip_label=SN74LS08N]
  R32 = Resistor [tolerance=±5% resistance=330 package=THT]
  R33 = Resistor [tolerance=±5% resistance=330 package=THT]
  R34 = Resistor [tolerance=±5% resistance=330 package=THT]
  R35 = Resistor [tolerance=±5% resistance=330 package=THT]
  R36 = Resistor [tolerance=±5% resistance=330 package=THT]
  R37 = Resistor [tolerance=±5% resistance=330 package=THT]
  R38 = Resistor [tolerance=±5% resistance=330 package=THT]
  R39 = Resistor [tolerance=±5% resistance=330 package=THT]
  R40 = Resistor [tolerance=±5% resistance=1k package="2010 [SMD]"]
  R41 = Resistor [tolerance=±5% resistance=1k package="2010 [SMD]"]
  R43 = Resistor [tolerance=±5% resistance=2.2k package="2010 [SMD]"]
  R44 = Resistor [tolerance=±5% resistance=1k package="2010 [SMD]"]
  R45 = Resistor [tolerance=±5% resistance=47k package="2010 [SMD]"]
  R46 = Resistor [tolerance=±5% resistance=1k package="2010 [SMD]"]
  R47 = Resistor [tolerance=±5% resistance=1k package="2010 [SMD]"]
  R48 = Resistor [tolerance=±5% resistance=2.2k package="2010 [SMD]"]
  C6 = Electrolytic Capacitor [capacitance=22µF voltage=35V package="0605 [SMD, electrolytic]"]
  C8 = Electrolytic Capacitor [capacitance=100µF voltage=50V package="300 mil [THT, electrolytic]"]
  C9 = Electrolytic Capacitor [capacitance=100µF voltage=50V package="300 mil [THT, electrolytic]"]
  S2 = Momentary Switch [package=tactile-pth]
  LED3 = LED - 5mm [color="Red (633nm)" package="5 mm [THT]"]
  LED5 = LED - 5mm [color="Red (633nm)" package="5 mm [THT]"]
  LED6 = LED - 5mm [color="Red (633nm)" package="5 mm [THT]"]
  LED4 = LED - 5mm [color="Red (633nm)" package="5 mm [THT]"]
  LED7 = LED - 5mm [color="Red (633nm)" package="5 mm [THT]"]
  LED8 = LED - 5mm [color="Red (633nm)" package="5 mm [THT]"]
  LED2 = LED - 5mm [color="Red (633nm)" package="5 mm [THT]"]
  LED1 = LED - 5mm [color="Yellow (595nm)" package="5 mm [THT]"]
  R42 = Resistor [tolerance=±5% resistance=3.3k package="2010 [SMD]"]

nets:
  GND: IC3.GND, U15.Ground, U16.Ground, U17.Ground, U18.pin8, U19.pin4, U19.pin5, U19.pin8, U20.pin7, U22.pin7, U21.pin7, C6.-, C8.-, C9.-, S2.1, S2.2
  +12V: IC3.IN
  VCC: IC3.OUT, U15.Vcc_Supply_Voltage, U16.Vcc_Supply_Voltage, U17.Reset, U17.Vcc_Supply_Voltage, U18.pin1, U18.pin7, U18.pin9, U18.pin10, U18.pin16, U19.pin6, U19.pin16, U20.pin14, U22.pin14, U21.pin14, R32.Pin_1, R33.Pin_1, R34.Pin_1, R35.Pin_1, R36.Pin_1, R37.Pin_1, R38.Pin_1, R39.Pin_1, R40.Pin_1, R41.Pin_1, R43.Pin_0, R44.Pin_0, R45.Pin_1, R46.Pin_1, R48.Pin_0
  N1: U15.Trigger, U15.Threshold, R47.Pin_0, C6.+
  N2: U15.Output, U18.pin2
  N3: U15.Reset, U20.pin2, U20.pin3, R46.Pin_0
  N4: U15.Discharge, R47.Pin_1, R48.Pin_1
  N5: U16.Trigger, U16.Threshold, C9.+, R42.Pin_0
  N6: U16.Output, U20.pin5
  N7: U16.Reset, U20.pin4, U20.pin8, R41.Pin_0
  N8: U16.Discharge, R43.Pin_1, R42.Pin_1
  N9: U17.Trigger, R44.Pin_1, S2.4
  N10: U17.Output, U20.pin1
  N11: U17.Threshold, U17.Discharge, R45.Pin_0, C8.+
  N12: U18.pin12, U19.pin3
  N13: U18.pin13, U19.pin2
  N14: U18.pin14, U19.pin1
  N15: U19.pin7, U21.pin12
  N16: U19.pin9, U21.pin9
  N17: U19.pin10, U21.pin4
  N18: U19.pin11, U21.pin2
  N19: U19.pin12, U20.pin9, U22.pin12
  N20: U19.pin13, U22.pin9
  N21: U19.pin14, U22.pin4
  N22: U19.pin15, U22.pin2
  N23: U20.pin6, U22.pin1, U22.pin5, U22.pin10, U22.pin13, U21.pin1, U21.pin5, U21.pin10, U21.pin13, R40.Pin_0
  N24: U22.pin3, LED8.cathode
  N25: U22.pin6, LED7.cathode
  N26: U22.pin8, LED6.cathode
  N27: U22.pin11, LED5.cathode
  N28: U21.pin3, LED4.cathode
  N29: U21.pin6, LED3.cathode
  N30: U21.pin8, LED2.cathode
  N31: U21.pin11, LED1.cathode
  N32: R32.Pin_0, LED8.anode
  N33: R33.Pin_0, LED4.anode
  N34: R34.Pin_0, LED3.anode
  N35: R35.Pin_0, LED2.anode
  N36: R36.Pin_0, LED1.anode
  N37: R37.Pin_0, LED5.anode
  N38: R38.Pin_0, LED6.anode
  N39: R39.Pin_0, LED7.anode
